// Logisim project BancDeRegistres.circ as structural Verilog: 1 circuit, main circuit BancRegistre
module BancRegistre (
  input  [2:0] RegA,
  input  [2:0] RegB,
  input  [31:0] DataIn,
  input  [2:0] RegDest,
  input  Clk,
  input  Reset,
  output [31:0] AOut,
  output [31:0] BOut,
  output [31:0] R0,
  output [31:0] R1,
  output [31:0] R2,
  output [31:0] R3,
  output [31:0] R4,
  output [31:0] R5,
  output [31:0] R6,
  output [31:0] R7
);

  Register #(.width(32)) register_1 (.clk(Clk), .clr(Reset));  // open: D, en, Q
  Register #(.width(32)) register_2 (.clk(Clk), .clr(Reset));  // open: D, en, Q
  Register #(.width(32)) register_3 (.clk(Clk), .clr(Reset));  // open: D, en, Q
  Register #(.width(32)) register_4 (.clk(Clk), .clr(Reset));  // open: D, en, Q
  Register #(.width(32)) register_5 (.clk(Clk), .clr(Reset));  // open: D, en, Q
  Register #(.width(32)) register_6 (.clk(Clk), .clr(Reset));  // open: D, en, Q
  Register #(.width(32)) register_7 (.clk(Clk), .clr(Reset));  // open: D, en, Q
  Register #(.width(32)) register_8 (.clk(Clk), .clr(Reset));  // open: D, en, Q
endmodule
