// Logisim project Ctl_Conditional.circ as structural Verilog: 1 circuit, main circuit Conditional
module Conditional (
  input  [15:0] Instruction,
  input  Z,
  input  C,
  input  N,
  input  V,
  input  Enable,
  output [10:0] Offset,
  output Verified
);

  wire condCCLO, condCSHS, condGE, condGT, condHI, condLE, condLS, condLT, condMI, condNE, condPL, condVC,
       condVS, multiplexer_1_out, or_1_out;
  wire [10:0] bit_extender_1_out, multiplexer_2_out;

  Multiplexer #(.select(4)) multiplexer_1 (
    .in0(Z), .in1(condNE), .in2(condCSHS), .in3(condCCLO), .in4(condMI), .in5(condPL), .in6(condVS),
    .in7(condVC), .in8(condHI), .in9(condLS), .in10(condGE), .in11(condLT), .in12(condGT), .in13(condLE),
    .in14(1'b1), .out(multiplexer_1_out), .sel(Instruction[11:8]));  // open: in15
  // Probe on Instruction[11:8]
  or or_1 (or_1_out, Instruction[13], multiplexer_1_out);
  assign bit_extender_1_out = {{3{Instruction[7]}}, Instruction[7:0]};  // Bit_Extender bit_extender_1
  and and_1 (Verified, Enable, or_1_out);
  Multiplexer #(.width(11)) multiplexer_2 (
    .in0(bit_extender_1_out), .in1(Instruction[10:0]), .out(multiplexer_2_out), .sel(Instruction[13]));
  and and_2 (condCSHS, C, 1'b1);
  and and_3 (condMI, N, 1'b1);
  and and_4 (condVS, V, 1'b1);
  and and_5 (condHI, condCSHS, condNE);
  or or_2 (condLS, condCCLO, Z);
  not not_1 (condLT, condGE);
  and and_6 (condGT, condGE, condNE);
  or or_3 (condLE, Z, condLT);
  Pull_Resistor pull_resistor_1 (.node(Offset));
  Multiplexer #(.width(11)) multiplexer_3 (.in0({11{1'b0}}), .in1(multiplexer_2_out), .out(Offset), .sel(Verified));
  not not_2 (condNE, Z);
  xnor xnor_1 (condCCLO, C, 1'b0);
  xnor xnor_2 (condPL, N, 1'b0);
  xnor xnor_3 (condVC, V, 1'b0);
  xnor xnor_4 (condGE, N, V);

  // Other names for the same wires on the sheet: condEQ = Z; imm8[7:0] = Instruction[7:0];
  //   imm11[10:0] = Instruction[10:0]; isCond[3:0] = Instruction[11:8]; isIncond = Instruction[13];
  //   isEnabled = Enable
endmodule
