// Logisim project Ctl_Data_Processing.circ as structural Verilog: 2 circuits, main circuit Data_Processing
module Data_Processing (
  input  Enable,
  input  [2:0] in_2,
  input  [15:0] Instruction,
  input  [3:0] in_4,
  output [2:0] Rn,
  output [2:0] Rd,
  output [2:0] Rm,
  output [3:0] ALU_Opcode,
  output [3:0] Flags_Update_Mask
);

  wire comparator_1_eq, comparator_2_eq, reverseRmRn;
  wire [2:0] rmValue;
  wire [3:0] multiplexer_3_out;

  Multiplexer #(.width(3)) multiplexer_1 (.in0(in_2), .in1(Instruction[2:0]), .out(Rd), .sel(Enable));
  Multiplexer #(.width(3)) multiplexer_2 (.in0(in_2), .in1(Instruction[5:3]), .out(rmValue), .sel(Enable));
  Multiplexer #(.select(4), .width(4)) multiplexer_3 (
    .in0(4'b1110), .in1(4'b1110), .in2(4'b1110), .in3(4'b1110), .in4(4'b1110), .in5(4'b1111), .in6(4'b1111),
    .in7(4'b1110), .in8(4'b1110), .in9(4'b1111), .in10(4'b1111), .in11(4'b1111), .in12(4'b1110),
    .in13(4'b1100), .in14(4'b1110), .in15(4'b1110), .out(multiplexer_3_out), .sel(Instruction[9:6]));
  Multiplexer #(.width(4)) multiplexer_4 (.in0(in_4), .in1(Instruction[9:6]), .out(ALU_Opcode), .sel(Enable));
  Multiplexer #(.width(4)) multiplexer_5 (.in0(in_4), .in1(multiplexer_3_out), .out(Flags_Update_Mask), .sel(Enable));
  Comparator #(.width(4)) comparator_1 (.a(ALU_Opcode), .b(4'b1101), .eq(comparator_1_eq));  // open: gt, lt
  Comparator #(.width(4)) comparator_2 (.a(ALU_Opcode), .b(4'b1001), .eq(comparator_2_eq));  // open: gt, lt
  or or_1 (reverseRmRn, comparator_1_eq, comparator_2_eq);
  Multiplexer #(.width(3)) multiplexer_6 (.in0(Rd), .in1(rmValue), .out(Rn), .sel(reverseRmRn));
  Multiplexer #(.width(3)) multiplexer_7 (.in0(rmValue), .in1(Rd), .out(Rm), .sel(reverseRmRn));

  // Other names for the same wires on the sheet: aluOPCODE[3:0] = ALU_Opcode; rnValue[2:0] = Rd

  // Notes on the sheet:
  //   Enable: initial=0x1
  //   Note 2: RSB instruction has Rn as 1st operand.
  //   MUL instruction has Rn as 1st operand and Rdm as 2nd operand
  //   For simplification purposes, Rm is used for 1st operand both here and in the ALU.
  //   Note: instructions that does not save the result will still have the second operand as the destination register, the ALU will copy the second register to the destination register
  //   Pull output low on Enable = 0
endmodule

module ALU (
  input  [31:0] A,
  input  [31:0] B,
  input  [4:0] Shift,
  input  CarryIn,
  input  [3:0] Codop,
  output [31:0] S,
  output [3:0] Flags
);

  wire bitselector_1_out, bitselector_2_out, bitselector_3_out, bitselector_4_out, bitselector_5_out,
       bitselector_6_out, bitselector_7_out, bitselector_8_out, bitselector_9_out, bitselector_10_out,
       bitselector_11_out, bitselector_12_out, cinq, comparator_2_eq, comparator_3_eq, comparator_4_eq,
       comparator_5_eq, comparator_6_eq, comparator_7_eq, douze, flagVforAdd, flagVforReverseSub,
       flagVforSub, huit, not_2_out, not_3_out, not_4_out, not_5_out, not_6_out, onze, quatre, sept, six,
       trois;
  wire [31:0] adder_1_out, and_1_out, multiplier_1_out, nand_1_out, negator_1_out, not_1_out, or_1_out,
       shifter_1_out, shifter_2_out, shifter_3_out, shifter_4_out, subtractor_1_out, xor_1_out;

  assign not_1_out = ~A;  // NOT_Gate not_1, 32 bits wide
  assign and_1_out = A & B;  // AND_Gate and_1, 32 bits wide
  assign xor_1_out = A ^ B;  // XOR_Gate xor_1, 32 bits wide
  Shifter #(.width(32)) shifter_1 (.in(B), .\dist (Shift), .out(shifter_1_out));
  Shifter #(.shift("lr"), .width(32)) shifter_2 (.in(B), .\dist (Shift), .out(shifter_2_out));
  Shifter #(.shift("ar"), .width(32)) shifter_3 (.in(B), .\dist (Shift), .out(shifter_3_out));
  Adder #(.width(32)) adder_1 (.a(A), .b(B), .out(adder_1_out), .cin(CarryIn), .cout(six));
  Subtractor #(.width(32)) subtractor_1 (.a(B), .b(A), .out(subtractor_1_out), .bin(CarryIn), .bout(sept));
  Shifter #(.shift("rr"), .width(32)) shifter_4 (.in(B), .\dist (Shift), .out(shifter_4_out));
  // AND_Gate and_2 has open pins: in0=B, in1=A, out=open
  Negator #(.width(32)) negator_1 (.in(A), .out(negator_1_out));
  Subtractor #(.width(32)) subtractor_2 (.a(B), .b(A), .bout(onze));  // open: out, bin
  Adder #(.width(32)) adder_2 (.a(B), .b(A), .cout(douze));  // open: out, cin
  assign or_1_out = B | A;  // OR_Gate or_1, 32 bits wide
  Multiplier #(.width(32)) multiplier_1 (.a(B), .b(A), .out(multiplier_1_out));  // open: cin, cout
  assign nand_1_out = ~(B & B);  // NAND_Gate nand_1, 32 bits wide
  Multiplexer #(.select(4), .width(32)) multiplexer_1 (
    .in0(and_1_out), .in1(xor_1_out), .in2(shifter_1_out), .in3(shifter_2_out), .in4(shifter_3_out),
    .in5(adder_1_out), .in6(subtractor_1_out), .in7(shifter_4_out), .in8(B), .in9(negator_1_out), .in10(B),
    .in11(B), .in12(or_1_out), .in13(multiplier_1_out), .in14(nand_1_out), .in15(not_1_out), .out(S),
    .sel(Codop));
  Comparator #(.width(32)) comparator_1 (.a(S), .b({32{1'b0}}), .eq(Flags[3]), .lt(Flags[2]));  // open: gt
  BitSelector #(.width(32)) bitselector_1 (.in(A), .out(bitselector_1_out), .sel({5{1'b1}}));
  BitSelector #(.width(32)) bitselector_2 (.in(B), .out(bitselector_2_out), .sel({5{1'b1}}));
  BitSelector #(.width(32)) bitselector_3 (.in(S), .out(bitselector_3_out), .sel({5{1'b1}}));
  BitSelector #(.width(32)) bitselector_4 (.in(B), .out(bitselector_4_out), .sel({5{1'b1}}));
  BitSelector #(.width(32)) bitselector_5 (.in(A), .out(bitselector_5_out), .sel({5{1'b1}}));
  BitSelector #(.width(32)) bitselector_6 (.in(B), .out(bitselector_6_out), .sel({5{1'b1}}));
  BitSelector #(.width(32)) bitselector_7 (.in(S), .out(bitselector_7_out), .sel({5{1'b1}}));
  BitSelector #(.width(32)) bitselector_8 (.in(B), .out(bitselector_8_out), .sel({5{1'b1}}));
  BitSelector #(.width(32)) bitselector_9 (.in(A), .out(bitselector_9_out), .sel({5{1'b1}}));
  BitSelector #(.width(32)) bitselector_10 (.in({32{1'b0}}), .out(bitselector_10_out), .sel({5{1'b1}}));
  BitSelector #(.width(32)) bitselector_11 (.in(S), .out(bitselector_11_out), .sel({5{1'b1}}));
  BitSelector #(.width(32)) bitselector_12 (.in({32{1'b0}}), .out(bitselector_12_out), .sel({5{1'b1}}));
  Comparator #(.width(1)) comparator_2 (
    .a(bitselector_1_out), .b(bitselector_2_out), .eq(comparator_2_eq));  // open: gt, lt
  not not_2 (not_2_out, comparator_3_eq);
  Comparator #(.width(1)) comparator_3 (
    .a(bitselector_3_out), .b(bitselector_4_out), .eq(comparator_3_eq));  // open: gt, lt
  Comparator #(.width(1)) comparator_4 (
    .a(bitselector_5_out), .b(bitselector_6_out), .eq(comparator_4_eq));  // open: gt, lt
  not not_3 (not_3_out, comparator_4_eq);
  not not_4 (not_4_out, comparator_5_eq);
  Comparator #(.width(1)) comparator_5 (
    .a(bitselector_7_out), .b(bitselector_8_out), .eq(comparator_5_eq));  // open: gt, lt
  Comparator #(.width(1)) comparator_6 (
    .a(bitselector_9_out), .b(bitselector_10_out), .eq(comparator_6_eq));  // open: gt, lt
  not not_5 (not_5_out, comparator_6_eq);
  not not_6 (not_6_out, comparator_7_eq);
  Comparator #(.width(1)) comparator_7 (
    .a(bitselector_11_out), .b(bitselector_12_out), .eq(comparator_7_eq));  // open: gt, lt
  and and_3 (flagVforAdd, comparator_2_eq, not_2_out);
  and and_4 (flagVforSub, not_3_out, not_4_out);
  and and_5 (flagVforReverseSub, not_5_out, not_6_out);
  Multiplexer #(.select(4)) multiplexer_2 (
    .in0(1'b0), .in1(1'b0), .in2(trois), .in3(quatre), .in4(cinq), .in5(six), .in6(sept), .in7(huit),
    .in8(1'b0), .in9(1'b1), .in10(onze), .in11(douze), .in12(1'b0), .in13(1'b0), .in14(1'b0), .in15(1'b0),
    .out(Flags[1]), .sel(Codop));
  BitSelector #(.width(32)) bitselector_13 (.in(B), .out(huit), .sel(Shift));
  BitSelector #(.width(32)) bitselector_14 (.in(B), .out(trois), .sel(Shift));
  BitSelector #(.width(32)) bitselector_15 (.in(B), .out(quatre));  // open: sel
  BitSelector #(.width(32)) bitselector_16 (.in(B), .out(cinq));  // open: sel
  Multiplexer #(.select(4)) multiplexer_3 (
    .in0(1'b0), .in1(1'b0), .in2(1'b0), .in3(1'b0), .in4(1'b0), .in5(flagVforAdd), .in6(flagVforSub),
    .in7(1'b0), .in8(1'b0), .in9(flagVforReverseSub), .in10(flagVforSub), .in11(flagVforAdd), .in12(1'b0),
    .in13(1'b0), .in14(1'b0), .in15(1'b0), .out(Flags[0]), .sel(Codop));

  // Other names for the same wires on the sheet: V = Flags[0]; CoutNS = Flags[1]; Sortie[31:0] = S

  // Notes on the sheet:
  //   Note: for ROR, C = N
  //   Note 2: assume that shift > 0 for LSL and LSR
  //   Flags
  //   Calcul de C
  //   CALCUL DE V
endmodule
