// Logisim project Ctl_Load_Store.circ as structural Verilog: 1 circuit, main circuit Load_Store
module Load_Store (
  input  Enable,
  input  [31:0] Stack_Pointer,
  input  [15:0] Instruction,
  input  Clk,
  input  Reset,
  output [2:0] Rmd,
  output [31:0] RAM_Addr,
  output Store,
  output Load,
  output PC_Hold
);

  wire and_2_out, d_ff_1_q, d_ff_1_qn, not_1_out, not_2_out, or_1_out;
  wire [2:0] bit_extender_3_out;
  wire [31:0] Address, bit_extender_1_out, bit_extender_2_out;

  assign bit_extender_1_out = {{31{Enable}}, Enable};  // Bit_Extender bit_extender_1
  assign RAM_Addr = Address & bit_extender_1_out;  // AND_Gate and_1, 32 bits wide
  assign bit_extender_2_out = {{24{Instruction[7]}}, Instruction[7:0]};  // Bit_Extender bit_extender_2
  Adder #(.width(32)) adder_1 (.a(bit_extender_2_out), .b(Stack_Pointer), .out(Address));  // open: cin, cout
  not not_1 (not_1_out, d_ff_1_q);
  D_Flip_Flop #(.trigger("falling")) d_ff_1 (
    .D(and_2_out), .clk(Clk), .Q(d_ff_1_q), .Qn(d_ff_1_qn), .reset(or_1_out));  // open: preset
  and and_2 (and_2_out, not_1_out, Instruction[11]);
  or or_1 (or_1_out, ~Instruction[11], Reset, ~Enable);  // OR_Gate
  and and_3 (Load, Enable, Instruction[11], d_ff_1_q);
  and and_4 (PC_Hold, d_ff_1_qn, Instruction[11], Enable);
  assign bit_extender_3_out = {{2{Enable}}, Enable};  // Bit_Extender bit_extender_3
  assign Rmd = Instruction[10:8] & bit_extender_3_out;  // AND_Gate and_5, 3 bits wide
  not not_2 (not_2_out, Instruction[11]);
  and and_6 (Store, Enable, not_2_out);

  // Other names for the same wires on the sheet: Imm8[7:0] = Instruction[7:0]; opCode[2:0] = Instruction[10:8];
  //   bitPoidsFort = Instruction[11]; isEnabled = Enable

  // Notes on the sheet:
  //   Instruction: pull=down
  //   Delay load and hold PC for 1 cycle for the RAM to send out requested data 
endmodule
