// Logisim project Ctl_Opcode_Decoder.circ as structural Verilog: 1 circuit, main circuit Opcode_Decoder
module Opcode_Decoder (
  input  [5:0] Opcode,
  output Shift,
  output Data_Processing,
  output Load_Store,
  output SP_Address,
  output Conditional
);

  wire comparator_2_eq, comparator_3_eq;
  wire [1:0] bitselector_1_out;
  wire [5:0] shifter_1_out, shifter_2_out, shifter_3_out, shifter_4_out;

  Shifter #(.shift("lr"), .width(6)) shifter_1 (.in(Opcode), .\dist (3'b010), .out(shifter_1_out));
  BitSelector #(.group(2), .width(6)) bitselector_1 (.in(Opcode), .out(bitselector_1_out), .sel(2'b10));
  Shifter #(.shift("lr"), .width(6)) shifter_2 (.in(Opcode), .\dist (3'b010), .out(shifter_2_out));
  Shifter #(.shift("lr"), .width(6)) shifter_3 (.in(Opcode), .\dist (3'b001), .out(shifter_3_out));
  Shifter #(.shift("lr"), .width(6)) shifter_4 (.in(Opcode), .\dist (3'b010), .out(shifter_4_out));
  Comparator #(.width(6)) comparator_1 (.a(shifter_1_out), .b(6'b001011), .eq(SP_Address));  // open: gt, lt
  Comparator #(.width(6)) comparator_2 (.a(shifter_3_out), .b(6'b011100), .eq(comparator_2_eq));  // open: gt, lt
  Comparator #(.width(6)) comparator_3 (.a(shifter_4_out), .b(6'b001101), .eq(comparator_3_eq));  // open: gt, lt
  Comparator #(.width(2)) comparator_4 (.a(bitselector_1_out), .b(2'b00), .eq(Shift));  // open: gt, lt
  Comparator #(.width(6)) comparator_5 (.a(Opcode), .b(6'b010000), .eq(Data_Processing));  // open: gt, lt
  Comparator #(.width(6)) comparator_6 (.a(shifter_2_out), .b(6'b001001), .eq(Load_Store));  // open: gt, lt
  or or_1 (Conditional, comparator_2_eq, comparator_3_eq);

  // Notes on the sheet:
  //   Shift, add, sub, mov
  //   Load/Store
  //   SP Address
  //   Data Processing
  //   Conditional branch
endmodule
