// Logisim project Ctl_SP_Address.circ as structural Verilog: 1 circuit, main circuit SP_Address
module SP_Address (
  input  [31:0] Stack_Pointer,
  input  [15:0] Instruction,
  input  Enable,
  output [31:0] New_Stack_Pointer,
  output Write_Enable
);

  wire [31:0] bit_extender_1_out, bit_extender_2_out, bit_extender_3_out, newSp, shouldAdd, shouldSub;

  assign bit_extender_1_out = {{25{1'b0}}, Instruction[6:0]};  // Bit_Extender bit_extender_1
  Adder #(.width(32)) adder_1 (.a(bit_extender_1_out), .b(Stack_Pointer), .out(shouldAdd));  // open: cin, cout
  assign bit_extender_2_out = {{31{Enable}}, Enable};  // Bit_Extender bit_extender_2
  assign bit_extender_3_out = {{25{1'b0}}, Instruction[6:0]};  // Bit_Extender bit_extender_3
  assign New_Stack_Pointer = newSp & bit_extender_2_out;  // AND_Gate and_1, 32 bits wide
  Subtractor #(.width(32)) subtractor_1 (
    .a(Stack_Pointer), .b(bit_extender_3_out), .out(shouldSub));  // open: bin, bout
  Multiplexer #(.width(32)) multiplexer_1 (.in0(shouldAdd), .in1(shouldSub), .out(newSp), .sel(Instruction[7]));

  assign Write_Enable = Enable;

  // Other names for the same wires on the sheet: imm7[6:0] = Instruction[6:0]; operation = Instruction[7];
  //   sp[31:0] = Stack_Pointer

  // Notes on the sheet:
  //   Pull output low on Enable = 0
endmodule
