// Logisim project Ctl_Shift_Add_Sub_Mov.circ as structural Verilog: 6 circuits, main circuit Shift_Add_Sub_Mov
module Shift_Add_Sub_Mov (
  input  Enable,
  input  [15:0] Instruction,
  output [3:0] Flags_Update_Mask,
  output Carry,
  output [2:0] Rm,
  output [2:0] Rn,
  output [2:0] Rd,
  output [4:0] Imm5,
  output [31:0] Imm32,
  output Imm32_Enable,
  output [3:0] ALU_Opcode
);

  wire and_1_out, comparator_1_eq, comparator_2_eq, comparator_3_eq, comparator_4_eq, comparator_5_eq,
       not_1_out, not_2_out, or_1_out, tvaluopcode_1_s1, tvrmouimm3_1_s1;
  wire [1:0] Operation;
  wire [2:0] multiplexer_7_out, multiplexer_8_out;
  wire [3:0] MaskFlags, multiplexer_1_out, OpCode, tvopcode_1_mask, tvopcodecomplexe_1_mask2;
  wire [4:0] multiplexer_9_out;
  wire [31:0] bit_extender_1_out, bit_extender_2_out, multiplexer_4_out, multiplexer_5_out,
       multiplexer_6_out, negator_1_out;

  Comparator #(.width(3)) comparator_1 (.a(Instruction[13:11]), .b(3'b100), .eq(comparator_1_eq));  // open: gt, lt
  TVALuOpCode tvaluopcode_1 (.e1(Operation), .s1(tvaluopcode_1_s1));
  TableVerite tableverite_1 (.e1(Instruction[13]), .e2(Instruction[12]), .e3(Instruction[11]), .s1(Operation));
  TVOpCode tvopcode_1 (.e1(Instruction[13]), .e2(Instruction[12]), .e3(Instruction[11]), .mask(tvopcode_1_mask));
  Multiplexer #(.width(4)) multiplexer_1 (
    .in0(4'b1110), .in1(4'b1111), .out(multiplexer_1_out), .sel(tvaluopcode_1_s1));
  TVOpCodeComplexe tvopcodecomplexe_1 (.e(Instruction[10:9]), .mask2(tvopcodecomplexe_1_mask2));
  Comparator #(.width(4)) comparator_2 (.a(tvopcode_1_mask), .b(4'b0111), .eq(comparator_2_eq));  // open: gt, lt
  Multiplexer #(.width(4)) multiplexer_2 (
    .in0(multiplexer_1_out), .in1(4'b1100), .out(MaskFlags), .sel(comparator_1_eq));
  not not_1 (not_1_out, comparator_2_eq);
  not not_2 (not_2_out, Instruction[13]);
  Multiplexer #(.width(4)) multiplexer_3 (
    .in0(tvopcodecomplexe_1_mask2), .in1(tvopcode_1_mask), .out(OpCode), .sel(not_1_out));
  assign bit_extender_1_out = {{24{1'b0}}, Instruction[7:0]};  // Bit_Extender bit_extender_1
  and and_1 (and_1_out, Instruction[10], Instruction[11], Instruction[12], not_2_out);
  assign bit_extender_2_out = {{29{1'b0}}, Instruction[8:6]};  // Bit_Extender bit_extender_2
  TVRmOUImm3 tvrmouimm3_1 (.binsup(Instruction[10:9]), .s1(tvrmouimm3_1_s1));
  Negator #(.width(32)) negator_1 (.in(bit_extender_1_out), .out(negator_1_out));
  Comparator #(.width(3)) comparator_3 (.a(Instruction[13:11]), .b(3'b100), .eq(comparator_3_eq));  // open: gt, lt
  or or_1 (or_1_out, Instruction[13], and_1_out);
  Multiplexer #(.width(32)) multiplexer_4 (
    .in0({32{1'b0}}), .in1(bit_extender_2_out), .out(multiplexer_4_out), .sel(tvrmouimm3_1_s1));
  Multiplexer #(.width(32)) multiplexer_5 (
    .in0(bit_extender_1_out), .in1(negator_1_out), .out(multiplexer_5_out), .sel(comparator_3_eq));
  Multiplexer #(.select(2), .width(32)) multiplexer_6 (
    .in0({32{1'b0}}), .in1(multiplexer_4_out), .in2(multiplexer_5_out), .in3({32{1'b0}}),
    .out(multiplexer_6_out), .sel(Operation));
  Comparator #(.width(4)) comparator_4 (.a(OpCode), .b(4'b0110), .eq(comparator_4_eq));  // open: gt, lt
  Multiplexer #(.select(2), .width(3)) multiplexer_7 (
    .in0(Instruction[5:3]), .in1(Instruction[5:3]), .in2(Instruction[10:8]), .in3(3'b000),
    .out(multiplexer_7_out), .sel(Operation));
  Multiplexer #(.select(2), .width(3)) multiplexer_8 (
    .in0(Instruction[2:0]), .in1(Instruction[2:0]), .in2(Instruction[10:8]), .in3(3'b000),
    .out(multiplexer_8_out), .sel(Operation));
  Multiplexer #(.select(2), .width(5)) multiplexer_9 (
    .in0(Instruction[10:6]), .in1({5{1'b0}}), .in2({5{1'b0}}), .in3({5{1'b0}}), .out(multiplexer_9_out),
    .sel(Operation));
  Comparator #(.width(32)) comparator_5 (.a(multiplexer_6_out), .b({32{1'b0}}), .eq(comparator_5_eq));  // open: gt, lt
  Multiplexer #(.width(4)) multiplexer_10 (.in0(4'b0000), .in1(MaskFlags), .out(Flags_Update_Mask), .sel(Enable));
  Multiplexer multiplexer_11 (.in0(1'b0), .in1(comparator_4_eq), .out(Carry), .sel(Enable));
  Multiplexer #(.width(3)) multiplexer_12 (.in0(3'b000), .in1(Instruction[8:6]), .out(Rm), .sel(Enable));
  Multiplexer #(.width(3)) multiplexer_13 (.in0(3'b000), .in1(multiplexer_7_out), .out(Rn), .sel(Enable));
  Multiplexer #(.width(3)) multiplexer_14 (.in0(3'b000), .in1(multiplexer_8_out), .out(Rd), .sel(Enable));
  Multiplexer #(.width(5)) multiplexer_15 (.in0({5{1'b0}}), .in1(multiplexer_9_out), .out(Imm5), .sel(Enable));
  Multiplexer #(.width(32)) multiplexer_16 (.in0({32{1'b0}}), .in1(multiplexer_6_out), .out(Imm32), .sel(Enable));
  Multiplexer #(.width(4)) multiplexer_17 (.in0(4'b0000), .in1(OpCode), .out(ALU_Opcode), .sel(Enable));
  Multiplexer multiplexer_18 (.in0(1'b0), .in1(or_1_out), .out(Imm32_Enable), .sel(Enable));

  // Other names for the same wires on the sheet: Bin[2:0] = Instruction[13:11]; imm5_t[4:0] = Instruction[10:6];
  //   imm8[7:0] = Instruction[7:0]; RmEqualsOUimm3[2:0] = Instruction[8:6]; RdSupp[2:0] = Instruction[10:8];
  //   BinSupp[1:0] = Instruction[10:9]; RdSubEquals[2:0] = Instruction[2:0]; Rn_t[2:0] = Instruction[5:3]

  // Notes on the sheet:
  //   Note: ALU uses Rn register for shifts. Use Rn instead of Rm for shifts (immediate) here too
  //   Note 2: MOV uses RSB ALU opcode with Imm8 reversed so that it is copied to output register
  //   Note 3: Imm32_Enable forces the use of the immediate for Rm register
  //   #100 code de mov qui ne met a jour que N et Z
  //   Deux cas en dehors de mov soit N,Z,C soit N,Z,C,V
  //   Pull output low on Enable = 0
  //   OpCode 0110 pour carry = 1 sinon = 0
  //   Enable carry for SUB since it is reversed in ALU
  //   only ADD and SUB use Rm
  //   ALU will use Imm32 instead of Rm
endmodule

module TableVerite (
  input  e1,
  input  e2,
  input  e3,
  output [1:0] s1
);

  wire not_1_out;

  not not_1 (not_1_out, e1);
  and and_1 (s1[0], not_1_out, e2, e3);

  assign s1[1] = e1;
endmodule

module TVOpCode (
  input  e1,
  input  e2,
  input  e3,
  output [3:0] mask
);

  wire and_2_out, and_3_out, and_4_out, not_1_out, not_2_out, not_3_out;

  not not_1 (not_1_out, e1);
  not not_2 (not_2_out, e2);
  not not_3 (not_3_out, e3);
  and and_1 (mask[3], e1, not_2_out);
  and and_2 (and_2_out, not_1_out, not_2_out);
  and and_3 (and_3_out, not_1_out, e3);
  and and_4 (and_4_out, e1, not_3_out);
  or or_1 (mask[1], and_2_out, e3);
  or or_2 (mask[0], and_3_out, and_4_out);

  assign mask[2] = e2;
endmodule

module TVOpCodeComplexe (
  input  [1:0] e,
  output [3:0] mask2
);

  not not_1 (mask2[0], e[0]);

  assign mask2[3:1] = {2'b01, e[0]};
endmodule

module TVRmOUImm3 (
  input  [1:0] binsup,
  output s1
);


  assign s1 = binsup[1];
endmodule

module TVALuOpCode (
  input  [1:0] e1,
  output s1
);

  or or_1 (s1, e1[0], e1[1]);
endmodule
