// Logisim project Machine_Logisim3.circ as structural Verilog: 3 circuits, main circuit Facade
module Facade (
);

  wire and_1_out, and_2_out, and_3_out, and_4_out, and_5_out, and_6_out, BREAK, Clk, Clk_Button2,
       Clk_Button_out, clock_1_out, CONTINUE, d_ff_2_qn, decoder_1_out0, decoder_1_out1, decoder_1_out2,
       decoder_1_out3, decoder_1_out4, decoder_1_out5, KEYB_Eof, KEYB_Read, KEYB_ReadEn, MMIO_En, or_1_out,
       or_4_out, Reset, RNG_Read, Rst_Button_out, RST_Signal, Store, TTY_Upd;
  wire [3:0] binary_to_bcd_converter_1_p2, binary_to_bcd_converter_1_p3, binary_to_bcd_converter_1_p4,
       binary_to_bcd_converter_1_p5, CPU_1_flags, MMIO_Addr;
  wire [4:0] JOY_X, JOY_Y;
  wire [6:0] KEYB_Char, TTY_Char;
  wire [7:4] RAM_Addr;
  wire [15:0] multiplier_1_out, ROM_Addr, ROMa_data;
  wire [31:0] bcd8digits_1_bcd, CPU_1_r0, CPU_1_r1, CPU_1_r2, CPU_1_r3, CPU_1_r6, CPU_1_r7, CPU_1_sp, Dip1,
       Dip2, Dip3, divider_1_out, divider_1_rem, MMIO_Out, multiplexer_1_out, R4, R5, RAM_Out, RAMa_dout,
       random_1_out, register_3_q, Res, Screen;
  wire [31:1] undriven_2;
  wire [31:5] undriven_4, undriven_5;
  wire [31:7] undriven, undriven_3;
  wire [31:9] CPU_1_ram_addr;

  DipSwitch dipswitch_1 (
    .sw1(Dip1[7]), .sw2(Dip1[6]), .sw3(Dip1[5]), .sw4(Dip1[4]), .sw5(Dip1[3]), .sw6(Dip1[2]), .sw7(Dip1[1]),
    .sw8(Dip1[0]));
  // Probe on Dip1[7:0]
  DipSwitch dipswitch_2 (
    .sw1(Dip2[7]), .sw2(Dip2[6]), .sw3(Dip2[5]), .sw4(Dip2[4]), .sw5(Dip2[3]), .sw6(Dip2[2]), .sw7(Dip2[1]),
    .sw8(Dip2[0]));
  Keyboard keyboard_1 (.clk(Clk), .re(KEYB_ReadEn), .clr(Reset), .avail(KEYB_Eof), .data(KEYB_Char));
  and and_1 (and_1_out, MMIO_En, Store);
  Decoder #(.select(4)) decoder_1 (
    .out0(decoder_1_out0), .out1(decoder_1_out1), .out2(decoder_1_out2), .out3(decoder_1_out3),
    .out4(decoder_1_out4), .out5(decoder_1_out5), .sel(MMIO_Addr), .en(and_1_out));  // open: out6, out7, out8, out9, out10, out11, out12, out13, out14, out15
  RAM #(.dataWidth(32)) RAMa (
    .addr({RAM_Addr, MMIO_Addr}), .we(and_2_out), .oe(1'b1), .clk(Clk), .din(RAM_Out), .dout(RAMa_dout));
  and and_2 (and_2_out, ~MMIO_En, Store);  // AND_Gate
  // Probe on Dip2[7:0]
  // Probe on MMIO_Addr
  // Probe on {MMIO_En, RAM_Addr, MMIO_Addr}
  // Probe on Dip3[7:0]
  DipSwitch dipswitch_3 (
    .sw1(Dip3[7]), .sw2(Dip3[6]), .sw3(Dip3[5]), .sw4(Dip3[4]), .sw5(Dip3[3]), .sw6(Dip3[2]), .sw7(Dip3[1]),
    .sw8(Dip3[0]));
  Joystick #(.bits(5)) joystick_1 (.x(JOY_X), .y(JOY_Y));
  Register #(.trigger("falling"), .width(7)) register_1 (
    .D(RAM_Out[6:0]), .en(decoder_1_out0), .clk(Clk), .Q(TTY_Char), .clr(Reset));
  Register #(.width(32)) register_2 (.D(RAM_Out), .en(decoder_1_out1), .clk(Clk), .Q(Res), .clr(Reset));
  Register #(.width(32)) register_3 (.D(RAM_Out), .en(decoder_1_out2), .clk(Clk), .Q(register_3_q), .clr(Reset));
  Register #(.width(1)) register_4 (.D(RAM_Out[0]), .en(decoder_1_out4), .clk(Clk), .Q(RST_Signal), .clr(Reset));
  Register #(.width(1)) register_5 (.D(RAM_Out[0]), .en(decoder_1_out5), .clk(Clk), .Q(BREAK), .clr(or_1_out));
  or or_1 (or_1_out, Reset, CONTINUE);
  Clock clock_1 (.out(clock_1_out));
  DotMatrix #(.inputtype("row"), .matrixcols(8), .matrixrows(4)) dotmatrix_1 (
    .row0(Screen[7:0]), .row1(Screen[15:8]), .row2(Screen[23:16]), .row3(Screen[31:24]));
  D_Flip_Flop d_ff_1 (.D(decoder_1_out0), .clk(Clk), .Q(TTY_Upd));  // open: Qn, preset, reset
  Register #(.width(32)) register_6 (.D(register_3_q), .en(and_3_out), .clk(Clk), .Q(Screen), .clr(Reset));
  and and_3 (and_3_out, RAM_Out[0], decoder_1_out3);
  or or_2 (Clk, and_4_out, Clk_Button_out, Clk_Button2);
  and and_4 (and_4_out, clock_1_out, ~BREAK);  // AND_Gate
  Button Clk_Button (.out(Clk_Button_out));
  Button Rst_Button (.out(Rst_Button_out));
  ROM #(.addrWidth(16), .dataWidth(16)) ROMa (.addr(ROM_Addr), .data(ROMa_data));
  or or_3 (Reset, Rst_Button_out, RST_Signal);
  // Probe on RAMa_dout
  Hex_Digit_Display hex_digit_display_1 (.value(Res[15:12]));  // open: dp
  D_Flip_Flop #(.trigger("falling")) d_ff_2 (.D(1'b0), .clk(Clk), .Qn(d_ff_2_qn), .preset(Reset));  // open: Q, reset
  DotMatrix #(.inputtype("row"), .matrixcols(32), .matrixrows(1)) dotmatrix_2 (.row0(Res));
  Hex_Digit_Display hex_digit_display_2 (.value(Res[11:8]));  // open: dp
  Hex_Digit_Display hex_digit_display_3 (.value(Res[7:4]));  // open: dp
  D_Flip_Flop d_ff_3 (.D(KEYB_Read), .clk(Clk), .Q(KEYB_ReadEn), .reset(or_4_out));  // open: Qn, preset
  or or_4 (or_4_out, ~KEYB_Read, Reset);  // OR_Gate
  Multiplexer #(.width(32)) multiplexer_1 (.in0(RAMa_dout), .in1(MMIO_Out), .out(multiplexer_1_out), .sel(MMIO_En));
  // Probe on multiplexer_1_out
  Button button_1 (.out(CONTINUE));
  Hex_Digit_Display hex_digit_display_4 (.value(Res[3:0]));  // open: dp
  // Probe on CPU_1_r1
  // Probe on CPU_1_r0
  and and_5 (and_5_out, Clk, d_ff_2_qn);
  Hex_Digit_Display hex_digit_display_5 (.value(binary_to_bcd_converter_1_p2));  // open: dp
  // Binary_to_BCD_converter #(.binvalue(13)) binary_to_bcd_converter_1: pin names not known; wires that end beside it: Res[12:0], binary_to_bcd_converter_1_p2, binary_to_bcd_converter_1_p3, binary_to_bcd_converter_1_p4, binary_to_bcd_converter_1_p5
  // Probe on CPU_1_r3
  // Probe on CPU_1_r2
  // Probe on R5
  // Probe on R4
  Button button_2 (.out(Clk_Button2));
  // Probe on Res
  Hex_Digit_Display hex_digit_display_6 (.value(binary_to_bcd_converter_1_p3));  // open: dp
  Hex_Digit_Display hex_digit_display_7 (.value(binary_to_bcd_converter_1_p4));  // open: dp
  Random #(.width(32)) random_1 (.next(RNG_Read), .clk(Clk), .out(random_1_out));  // open: clr
  // Probe on CPU_1_r7
  // Probe on CPU_1_r6
  // Probe on CPU_1_flags
  CPU CPU_1 (
    .RAM_In(multiplexer_1_out), .ROM_In(ROMa_data), .Clk(and_5_out), .Reset(Reset), .RAM_Out(RAM_Out),
    .ROM_Addr(ROM_Addr), .RAM_Addr({CPU_1_ram_addr, MMIO_En, RAM_Addr, MMIO_Addr}), .Store(Store),
    .Flags(CPU_1_flags), .SP(CPU_1_sp), .R0(CPU_1_r0), .R1(CPU_1_r1), .R2(CPU_1_r2), .R3(CPU_1_r3), .R4(R4),
    .R5(R5), .R6(CPU_1_r6), .R7(CPU_1_r7));
  Hex_Digit_Display hex_digit_display_8 (.value(binary_to_bcd_converter_1_p5));  // open: dp
  BCD8digits bcd8digits_1 (.Number(Res), .BCD(bcd8digits_1_bcd));
  Divider #(.width(32)) divider_1 (.a(R4), .b(R5), .out(divider_1_out), .rem(divider_1_rem));  // open: upper
  TTY tty_1 (.data(TTY_Char), .clk(Clk), .we(TTY_Upd), .clr(Reset));
  Multiplier #(.width(16)) multiplier_1 (.a(16'h2), .b(ROM_Addr), .out(multiplier_1_out));  // open: cin, cout
  // Probe on {MMIO_En, RAM_Addr, MMIO_Addr}
  // Probe on RAM_Out
  // Probe on CPU_1_sp
  Pull_Resistor pull_resistor_1 (.node(MMIO_Out));
  Multiplexer #(.select(4), .width(32)) multiplexer_2 (
    .in0({undriven, TTY_Char}), .in1(Res), .in2(register_3_q), .in3(Dip1), .in4(Dip2), .in5(Dip3),
    .in6({undriven_2, KEYB_Eof}), .in7({undriven_3, KEYB_Char}), .in8({undriven_4, JOY_X}),
    .in9({undriven_5, JOY_Y}), .in10(random_1_out), .in11(bcd8digits_1_bcd), .in12(divider_1_out),
    .in13(divider_1_rem), .out(MMIO_Out), .sel(MMIO_Addr));  // open: in14, in15
  // Probe on multiplier_1_out
  and and_6 (and_6_out, ~Store, MMIO_En);  // AND_Gate
  Decoder #(.select(4)) decoder_2 (
    .out7(KEYB_Read), .out10(RNG_Read), .sel(MMIO_Addr), .en(and_6_out));  // open: out0, out1, out2, out3, out4, out5, out6, out8, out9, out11, out12, out13, out14, out15

  // Other names for the same wires on the sheet: RAM_Addr (some bits) = {MMIO_En, MMIO_Addr}

  // Notes on the sheet:
  //   Entrées / Sorties mappées en mémoire
  //   Sorties
  //   contents of ROMa (hex, n*v repeats v):
  //   b09c b0ff b0f1 e7fe e7fe 2041 900c e7fe e7fe 203d 900c e7fe e7fe 2000 9005 e7fe e7fe e7fe 9812 2800
  //   d100 e7fe e7f9 e7fe 9813 9003 9803 9004 9804 280a d100 e7fe e015 9804 2830 db03 e7fe 9804 283a db00
  //   e7fe e7e4 e7fe 9804 900c e7fe 9805 210a 4341 9105 9804 9905 1808 3830 9005 e7d6 9805 9002 9802 9006
  //   e7fe 200a 900c 21*e7fe 206c 900c e7fe e7fe 2069 900c e7fe e7fe e7fe 2073 900c e7fe e7fe e7fe 2074
  //   900c e7fe e7fe e7fe 2065 900c e7fe e7fe e7fe 2020 900c e7fe e7fe e7fe 2064 900c e7fe e7fe e7fe 2065
  //   900c e7fe e7fe e7fe 2073 900c e7fe e7fe e7fe 2020 900c e7fe e7fe e7fe 2064 900c e7fe e7fe e7fe 2069
  //   900c e7fe e7fe e7fe 2076 900c e7fe e7fe e7fe 2069 900c e7fe e7fe e7fe 2073 900c e7fe e7fe e7fe 2065
  //   900c e7fe e7fe e7fe 2075 900c e7fe e7fe e7fe 2072 900c e7fe e7fe e7fe 2073 900c e7fe e7fe e7fe 203a
  //   900c e7fe e7fe 2000 9001 e7fe 9801 9906 4288 da56 e7fe 9806 9901 4 d 9819 9000 9800 2800 d147 e7fe
  //   9801 900d e7fe 9817 900b 980b 2800 d104 e7fe e7fe 2030 900c e7fe e033 980d 2800 da09 e7fe e7fe 202d
  //   900c e7fe 980d 4240 900d 9817 900b e7fe 2000 900a 9009 e7fe 9809 2807 d81d e7fe 980b 210f 4008 9008
  //   980b 900 900b 980a 2800 d108 e7fe 9808 2800 d002 e7fe 2001 900a e7ff e005 e7fe e7fe 9808 3030 900c
  //   e7fe e7fe 9809 1c40 9009 e7dc e7fe e7fe 202c 900c e7fe e7fe e7fe 9801 1c40 9001 e7a2 5*e7fe 200a
  //   900c e7fe e7fe 2073 900c e7fe e7fe e7fe 2074 900c e7fe e7fe e7fe 206f 900c e7fe e7fe e7fe 2070 900c
  //   4*e7fe 9812 2800 d100 e7fe e7f9 e7fe e7fe 2001 9010 e7fe e7fd
  //   Reprendre après un point d'arrêt
  //   Tic d'horloge
  //   Entrées
  //   PC effectif
endmodule

module CPU (
  input  [31:0] RAM_In,
  input  [15:0] ROM_In,
  input  Clk,
  input  Reset,
  output [31:0] R3,
  output [31:0] R7,
  output [31:0] R2,
  output [31:0] R6,
  output [31:0] R1,
  output [31:0] R5,
  output [31:0] R0,
  output [31:0] R4,
  output [31:0] RAM_Out,
  output [15:0] ROM_Addr,
  output [31:0] RAM_Addr,
  output Store,
  output [3:0] Flags,
  output [31:0] SP
);

  wire Controller_1_carry, Controller_1_dp_shift, Controller_1_imm32_enable, load;
  wire [2:0] Controller_1_rd, Controller_1_rm, Controller_1_rn;
  wire [3:0] Controller_1_alu_opcode, flags_t;
  wire [4:0] Controller_1_imm5, new_Shift;
  wire [31:0] A_Alu, ALU_1_s, BOut, Controller_1_imm32, dataIn_BDR;

  Controller Controller_1 (
    .FlagsIn(flags_t), .Clk(Clk), .Reset(Reset), .Inst(ROM_In), .DP_Shift(Controller_1_dp_shift),
    .Imm32_Enable(Controller_1_imm32_enable), .Imm5(Controller_1_imm5), .Imm32(Controller_1_imm32),
    .ALU_Opcode(Controller_1_alu_opcode), .Rm(Controller_1_rm), .Rn(Controller_1_rn), .Rd(Controller_1_rd),
    .Flags(Flags), .Carry(Controller_1_carry), .RAM_Addr(RAM_Addr), .Load(load), .Store(Store), .SP(SP),
    .PC(ROM_Addr));
  Multiplexer #(.width(5)) multiplexer_1 (
    .in0(RAM_Out[4:0]), .in1(Controller_1_imm5), .out(new_Shift), .sel(Controller_1_dp_shift));
  Multiplexer #(.width(32)) multiplexer_2 (
    .in0(RAM_Out), .in1(Controller_1_imm32), .out(A_Alu), .sel(Controller_1_imm32_enable));
  BancRegistre Regs_1 (
    .RegDest(Controller_1_rd), .DataIn(dataIn_BDR), .Clk(Clk), .Reset(Reset), .RegA(Controller_1_rm),
    .RegB(Controller_1_rn), .R3(R3), .R4(R4), .R5(R5), .R6(R6), .R7(R7), .R0(R0), .R1(R1), .R2(R2),
    .AOut(RAM_Out), .BOut(BOut));
  ALU ALU_1 (
    .CarryIn(Controller_1_carry), .A(A_Alu), .B(BOut), .Shift(new_Shift), .Codop(Controller_1_alu_opcode),
    .Flags(flags_t), .S(ALU_1_s));
  Multiplexer #(.width(32)) multiplexer_3 (.in0(ALU_1_s), .in1(RAM_In), .out(dataIn_BDR), .sel(load));

  // Other names for the same wires on the sheet: AOut[31:0] = RAM_Out
endmodule

module BCD8digits (
  input  [31:0] Number,
  output [31:0] BCD
);

  wire [31:0] divider_1_out, divider_2_out, divider_3_out, divider_4_out, divider_5_out, divider_6_out,
       divider_7_out;
  wire [31:4] divider_1_rem, divider_2_rem, divider_3_rem, divider_4_rem, divider_5_rem, divider_6_rem,
       divider_7_rem, divider_8_rem;

  Divider #(.width(32)) divider_1 (
    .a(Number), .b(32'ha), .out(divider_1_out), .rem({divider_1_rem, BCD[31:28]}));  // open: upper
  Divider #(.width(32)) divider_2 (
    .a(divider_1_out), .b(32'ha), .out(divider_2_out), .rem({divider_2_rem, BCD[27:24]}));  // open: upper
  Divider #(.width(32)) divider_3 (
    .a(divider_2_out), .b(32'ha), .out(divider_3_out), .rem({divider_3_rem, BCD[23:20]}));  // open: upper
  Divider #(.width(32)) divider_4 (
    .a(divider_3_out), .b(32'ha), .out(divider_4_out), .rem({divider_4_rem, BCD[19:16]}));  // open: upper
  Divider #(.width(32)) divider_5 (
    .a(divider_4_out), .b(32'ha), .out(divider_5_out), .rem({divider_5_rem, BCD[15:12]}));  // open: upper
  Divider #(.width(32)) divider_6 (
    .a(divider_5_out), .b(32'ha), .out(divider_6_out), .rem({divider_6_rem, BCD[11:8]}));  // open: upper
  Divider #(.width(32)) divider_7 (
    .a(divider_6_out), .b(32'ha), .out(divider_7_out), .rem({divider_7_rem, BCD[7:4]}));  // open: upper
  Divider #(.width(32)) divider_8 (.a(divider_7_out), .b(32'ha), .rem({divider_8_rem, BCD[3:0]}));  // open: out, upper
  // Probe on BCD
endmodule
